// Logisim project Calculadora binaria.circ as structural Verilog: 1 circuit, main circuit main
module main (
  input  [6:0] in_1,
  input  [6:0] in_2,
  input  in_3,
  input  [2:0] in_4,
  output [6:0] out_5
);

  wire [6:0] adder_1_out, and_1_out, divider_1_out, multiplexer_1_out, multiplier_1_out, not_1_out, or_1_out,
       subtractor_1_out, xor_1_out;

  Multiplexer #(.width(7), .enable("false")) multiplexer_1 (
    .in0(in_1), .in1(in_2), .out(multiplexer_1_out), .sel(in_3));
  Adder #(.width(7)) adder_1 (.a(in_1), .b(in_2), .out(adder_1_out));  // open: cin, cout
  Subtractor #(.width(7)) subtractor_1 (.a(in_1), .b(in_2), .out(subtractor_1_out));  // open: bin, bout
  Multiplier #(.width(7)) multiplier_1 (.a(in_1), .b(in_2), .out(multiplier_1_out));  // open: cin, cout
  Divider #(.width(7)) divider_1 (.a(in_1), .b(in_2), .out(divider_1_out));  // open: upper, rem
  assign and_1_out = in_1 & in_2;  // AND_Gate and_1, 7 bits wide
  assign or_1_out = in_1 | in_2;  // OR_Gate or_1, 7 bits wide
  assign xor_1_out = in_1 ^ in_2;  // XOR_Gate xor_1, 7 bits wide
  assign not_1_out = ~multiplexer_1_out;  // NOT_Gate not_1, 7 bits wide
  Multiplexer #(.select(3), .width(7), .enable("false")) multiplexer_2 (
    .in0(adder_1_out), .in1(subtractor_1_out), .in2(multiplier_1_out), .in3(divider_1_out), .in4(and_1_out),
    .in5(or_1_out), .in6(xor_1_out), .in7(not_1_out), .out(out_5), .sel(in_4));

  // Notes on the sheet:
  //   Número 1
  //   Número 2
  //   Pin de selección de numero al que se desea pasar por NOT
  //   Calculadora binaria
  //   Pin de selección de operación
  //   Resultado de operación
endmodule
